// Logisim project pruebas_programable.circ as structural Verilog: 1 circuit, main circuit main
module main (
);

  wire button_1_out, programmablecomponent_1_p4;

  Button button_1 (.out(button_1_out));
  // ProgrammableComponent programmablecomponent_1: pin names not known; wires that end beside it: 1'b1, button_1_out, 1'b1, programmablecomponent_1_p4
  LED led_1 (.in(programmablecomponent_1_p4));
endmodule
