// Logisim project c_running_simple.circ as structural Verilog: 3 circuits, main circuit main
module main (
);

  wire and_1_out, and_2_out, CLK_out, comparator_1_gt, control_1_alusrc, control_1_memwrite, control_1_op0,
       control_1_pcorreg, control_1_pcsrc, control_1_regwrite, not_1_out, riscvalu_1_p4, RST_out, tap_3_p1,
       tap_4_p1, tap_5_p1, tap_6_p1, tap_7_p1, tap_8_p2;
  wire [1:0] control_1_resultsrc;
  wire [2:0] control_1_alucontrol, control_1_immsrc, tap_2_p1;
  wire [6:0] tap_1_p2;
  wire [7:0] counter_1_q, registerfile32baremetal_1_p4, registerfile32baremetal_1_p4_2,
       registerfile32baremetal_1_p4_3, registerfile32baremetal_1_p4_4, tap_1_p1, tap_1_p1_2, tap_1_p1_3,
       tap_1_p1_4, undriven, undriven_2, undriven_3, undriven_4;
  wire [31:0] adder_1_out, adder_2_out, i_o_1_p4, multiplexer_1_out, multiplexer_2_out, multiplexer_3_out,
       multiplexer_4_out, multiplexer_5_out, PC_q, registerfile32baremetal_1_p1,
       registerfile32baremetal_1_p3, riscvalu_1_p5, riscvse_j_1_p4;

  Adder #(.width(32)) adder_1 (.a(PC_q), .b(32'h4), .out(adder_1_out));  // open: cin, cout
  Button RST (.out(RST_out));
  Clock CLK (.out(CLK_out));
  Multiplexer #(.width(32)) multiplexer_1 (
    .in0(adder_1_out), .in1(adder_2_out), .out(multiplexer_1_out), .sel(control_1_pcsrc));
  Register #(.width(32)) PC (.D(multiplexer_1_out), .Q(PC_q), .clk(CLK_out), .clr(RST_out));  // open: en
  // ROM #(.addrWidth(32), .line("quad")) rom_1: pin names not known; wires that end beside it: PC_q
  Counter counter_1 (.Q(counter_1_q), .up(1'b1), .clk(CLK_out), .clr(RST_out));  // open: load, D, count, carry
  // Probe on counter_1_q
  // Tap #(.incoming(32), .to(6)) tap_1: pin names not known; wires that end beside it: {tap_1_p1_4, tap_1_p1_3, tap_1_p1_2, tap_1_p1}, tap_1_p2
  // Tap #(.from(12), .incoming(32), .to(14)) tap_2: pin names not known; wires that end beside it: tap_2_p1
  // Tap #(.from(30), .incoming(32), .to(30)) tap_3: pin names not known; wires that end beside it: tap_3_p1
  // Tap #(.from(15), .incoming(32), .to(19)) tap_4: pin names not known; wires that end beside it: tap_4_p1, tap_4_p1
  // Tap #(.from(20), .incoming(32), .to(24)) tap_5: pin names not known; wires that end beside it: tap_5_p1, tap_5_p1
  // Tap #(.from(7), .incoming(32), .to(11)) tap_6: pin names not known; wires that end beside it: tap_6_p1, tap_6_p1
  // Tap #(.from(7), .incoming(32), .to(31)) tap_7: pin names not known; wires that end beside it: tap_7_p1
  control control_1 (
    .Funct7(tap_3_p1), .Funct3(tap_2_p1), .Zero(riscvalu_1_p4), .Op(tap_1_p2), .PCSrc(control_1_pcsrc),
    .PcOrReg(control_1_pcorreg), .ResultSrc(control_1_resultsrc), .MemWrite(control_1_memwrite),
    .ALUSrc(control_1_alusrc), .ImmSrc(control_1_immsrc), .RegWrite(control_1_regwrite), .Op0(control_1_op0),
    .ALUControl(control_1_alucontrol));  // open: O1
  // RegisterFile32Baremetal #(.clearToZero("false")) registerfile32baremetal_1: pin names not known; wires that end beside it: registerfile32baremetal_1_p1, control_1_regwrite, registerfile32baremetal_1_p3, {registerfile32baremetal_1_p4_4, registerfile32baremetal_1_p4_3, registerfile32baremetal_1_p4_2, registerfile32baremetal_1_p4}
  // RiscvSE_J riscvse_j_1: pin names not known; wires that end beside it: tap_7_p1, control_1_immsrc, RST_out, riscvse_j_1_p4, CLK_out
  Multiplexer #(.width(32)) multiplexer_2 (
    .in0(PC_q), .in1(registerfile32baremetal_1_p3), .out(multiplexer_2_out), .sel(control_1_pcorreg));
  Multiplexer #(.width(32)) multiplexer_3 (
    .in0(registerfile32baremetal_1_p3), .in1({32{1'b0}}), .out(multiplexer_3_out), .sel(control_1_op0));
  Multiplexer #(.width(32)) multiplexer_4 (
    .in0({registerfile32baremetal_1_p4_4, registerfile32baremetal_1_p4_3, registerfile32baremetal_1_p4_2, registerfile32baremetal_1_p4}),
    .in1(riscvse_j_1_p4), .out(multiplexer_4_out), .sel(control_1_alusrc));
  Comparator #(.mode("unsigned"), .width(32)) comparator_1 (
    .a(riscvalu_1_p5), .b(32'hffffffef), .gt(comparator_1_gt));  // open: eq, lt
  Adder #(.width(32)) adder_2 (.a(multiplexer_2_out), .b(riscvse_j_1_p4), .out(adder_2_out));  // open: cin, cout
  // RiscvALU riscvalu_1: pin names not known; wires that end beside it: multiplexer_3_out, multiplexer_4_out, control_1_alucontrol, riscvalu_1_p4, riscvalu_1_p5
  and and_1 (and_1_out, control_1_memwrite, comparator_1_gt);
  and and_2 (and_2_out, control_1_memwrite, not_1_out);
  not not_1 (not_1_out, comparator_1_gt);
  // Tap #(.incoming(32), .to(3)) tap_8: pin names not known; wires that end beside it: riscvalu_1_p5, tap_8_p2
  // RAM #(.addrWidth(32), .enables("line"), .line("quad"), .\type ("nonvolatile")) ram_1: pin names not known; wires that end beside it: riscvalu_1_p5, and_2_out, 1'b1, 1'b1, 1'b1, 1'b1, CLK_out, registerfile32baremetal_1_p4_4, registerfile32baremetal_1_p4_3, registerfile32baremetal_1_p4_2, registerfile32baremetal_1_p4
  // I_O i_o_1: pin names not known; wires that end beside it: tap_8_p2, {registerfile32baremetal_1_p4_4, registerfile32baremetal_1_p4_3, registerfile32baremetal_1_p4_2, registerfile32baremetal_1_p4}, and_1_out, i_o_1_p4
  Multiplexer #(.width(32)) multiplexer_5 (
    .in0({undriven_4, undriven_3, undriven_2, undriven}), .in1(i_o_1_p4), .out(multiplexer_5_out),
    .sel(comparator_1_gt));
  Multiplexer #(.select(2), .width(32)) multiplexer_6 (
    .in0(riscvalu_1_p5), .in1(multiplexer_5_out), .in2(adder_1_out), .out(registerfile32baremetal_1_p1));  // open: in3, sel

  // Notes on the sheet:
  //   contents of rom_1 (hex, n*v repeats v):
  //   3 40 0 ef fe 1 1 13 0 81 2e 23 2 1 4 13 fe a4 26 23 fe b4 24 23 0 0 27 83 fe 84 27 3 0 e7 a0 23 0 0
  //   0 13 1 c1 24 3 2 1 1 13 0 0 80 67 ff 1 1 13 0 11 26 23 0 81 24 23 1 1 4 13 0 0 27 3 0 40 27 83 0 7
  //   85 93 0 7 5 13 fb 1f f0 ef 0 0 7 93 0 7 85 13 0 c1 20 83 0 81 24 3 1 1 1 13 0 0 80 67
endmodule

module control (
  input  Zero,
  input  [6:0] Op,
  input  [2:0] Funct3,
  input  Funct7,
  output PCSrc,
  output PcOrReg,
  output [1:0] ResultSrc,
  output MemWrite,
  output ALUSrc,
  output [2:0] ImmSrc,
  output RegWrite,
  output Op0,
  output O1,
  output [2:0] ALUControl
);

  wire and_1_out, multiplexer_1_out, not_1_out, riscvmaindecoderext_1_p2, riscvmaindecoderext_1_p3,
       riscvmaindecoderext_1_p5, tap_1_p1, tap_2_p1;

  // Tap #(.from(5), .incoming(7), .to(5)) tap_1: pin names not known; wires that end beside it: tap_1_p1, Op
  // Tap #(.incoming(3)) tap_2: pin names not known; wires that end beside it: tap_2_p1, tap_1_p1
  not not_1 (not_1_out, Zero);
  Multiplexer multiplexer_1 (.in0(Zero), .in1(not_1_out), .out(multiplexer_1_out), .sel(tap_2_p1));
  // RiscvMainDecoderExt #(.behavior("long Op = state.getPortValue(nameToId.get(\"Op\")).toLongValue();\nlong Funct3 = state.getPortValue(nameToId.get(\"Funct3\")).toLongValue();\nlong RegWrite = 0, ImmSrc = 0, ALUSrc = 0, MemWrite = 0, ResultSrc = 0, Branch = 0, ALUOp = 0, O1 = 0, Op0=0, Jump=0, PcOrReg=0;\n\nif(Op == 0x3) { // lw\n    RegWrite = 1;\n    ALUSrc = 1;\n    ResultSrc = 1;\n} else if(Op == 0x23) { // sw\n    ImmSrc = 1;\n    ALUSrc = 1;\n    MemWrite = 1;\n} else if(Op == 0x33) { // R-type\n    RegWrite = 1;\n    ALUOp = 2;\n} else if(Op == 0x63) { // beq\n    ImmSrc = 2;\n    Branch = 1;\n    ALUOp = 1;\n} else if(Op == 0x13) { // addi\n    RegWrite = 1;\n    ALUSrc = 1;\n    ResultSrc = 0;\n    ALUOp = 2;\n} else if(Op == 0x37) { //lui\n     Op0=1;\n     RegWrite = 1;\n     ALUOp = 2;\n     ALUSrc = 1;\n     ImmSrc=3;\n} else if(Op == 0x6F) { //jal\n     RegWrite=1;\n     ImmSrc=4;\n     ResultSrc=2;\n     Jump=1;\n} else if(Op == 0x67) { //jalr\n     RegWrite=1;\n     ResultSrc=2;\n     Jump=1;\n     PcOrReg=1;\n}\n\nValue branchVal = Value.createKnown(BitWidth.create(1), Branch);\nstate.setPort(nameToId.get(\"Branch\"), branchVal, 1);\nValue resultSrcVal = Value.createKnown(BitWidth.create(2), ResultSrc);\nstate.setPort(nameToId.get(\"ResultSrc\"), resultSrcVal, 2);\nValue memWriteVal = Value.createKnown(BitWidth.create(1), MemWrite);\nstate.setPort(nameToId.get(\"MemWrite\"), memWriteVal, 1);\nValue aluSrcVal = Value.createKnown(BitWidth.create(1), ALUSrc);\nstate.setPort(nameToId.get(\"ALUSrc\"), aluSrcVal, 1);\nValue regWriteVal = Value.createKnown(BitWidth.create(1), RegWrite);\nstate.setPort(nameToId.get(\"RegWrite\"), regWriteVal, 1);\nValue immSrcVal = Value.createKnown(BitWidth.create(3), ImmSrc);\nstate.setPort(nameToId.get(\"ImmSrc\"), immSrcVal, 3);\nValue o1Val = Value.createKnown(BitWidth.create(1), O1);\nstate.setPort(nameToId.get(\"O1\"), o1Val, 1);\nValue op0Val = Value.createKnown(BitWidth.create(1), Op0);\nstate.setPort(nameToId.get(\"Op0\"), op0Val, 1);\nValue jumpVal = Value.createKnown(BitWidth.create(1), Jump);\nstate.setPort(nameToId.get(\"Jump\"), jumpVal, 1);\nValue pcOrRegVal = Value.createKnown(BitWidth.create(1), PcOrReg);\nstate.setPort(nameToId.get(\"PcOrReg\"), pcOrRegVal, 1);\nValue aluOpVal = Value.createKnown(BitWidth.create(2), ALUOp);\nstate.setPort(nameToId.get(\"ALUOp\"), aluOpVal, 2);")) riscvmaindecoderext_1: pin names not known; wires that end beside it: Funct3, riscvmaindecoderext_1_p2, riscvmaindecoderext_1_p3, PcOrReg, riscvmaindecoderext_1_p5, ResultSrc, MemWrite, ALUSrc, ImmSrc, RegWrite, Op0, O1
  // RiscvALUDecoder #(.behavior("long ALUOp = state.getPortValue(nameToId.get(\"ALUOp\")).toLongValue();\nlong Op = state.getPortValue(nameToId.get(\"Op\")).toLongValue();\nlong Funct3 = state.getPortValue(nameToId.get(\"Funct3\")).toLongValue();\nlong Funct7 = state.getPortValue(nameToId.get(\"Funct7\")).toLongValue();\n\nlong ans = 0;\n \nif (ALUOp == 0x0) { // ALUOp = 00 for lw/sw\n   ans = 0b000; // ALUControl = 000 (add) \n} else if (ALUOp == 0x1) { // ALUOp = 01 for beq\n   ans = 0b001; // ALUControl = 001 (subtract) \n} else if (ALUOp == 0x2) { // ALUOp = 10 for R-type instructions\n   if (Funct3 == 0x0) { \n      if(Op == 0x1 && Funct7 == 0x1) { \n         ans = 0b001; // ALUControl = 001 (subtract)\n      } else {\n         ans = 0b000; // ALUControl = 000 (add)\n      }  \n   } else if (Funct3 == 0x2) {   \n      ans = 0b101; // ALUControl = 101 (set less than)   \n   } else if (Funct3 == 0x6) {   \n      ans = 0b011; // ALUControl = 011 (or)   \n   } else if (Funct3 == 0x7) {   \n      ans = 0b010; // ALUControl = 010 (and)   \n   }   \n}   \n \nValue ALUControl = Value.createKnown(BitWidth.create(3), ans);   \n \nstate.setPort(nameToId.get(\"ALUControl\"), ALUControl, 3);")) riscvaludecoder_1: pin names not known; wires that end beside it: Funct3, Funct7, riscvmaindecoderext_1_p3, ALUControl
  and and_1 (and_1_out, multiplexer_1_out, riscvmaindecoderext_1_p5);
  or or_1 (PCSrc, riscvmaindecoderext_1_p2, and_1_out);
endmodule

// IO Module
module I_O (
  input  [3:0] Address,
  input  [31:0] DataIn,
  input  in_3,
  input  [31:0] in_4,
  input  [31:0] in_5,
  input  [31:0] in_6,
  input  [31:0] in_7,
  input  [31:0] in_8,
  input  [31:0] in_9,
  input  [31:0] in_10,
  input  [31:0] in_11,
  input  [31:0] in_12,
  input  [31:0] in_13,
  input  [31:0] in_14,
  input  [31:0] in_15,
  input  [31:0] in_16,
  input  [31:0] in_17,
  input  [31:0] in_18,
  input  [31:0] in_19,
  output [31:0] out_20,
  output [31:0] out_21,
  output [31:0] out_22,
  output [31:0] out_23,
  output [31:0] out_24,
  output [31:0] out_25,
  output [31:0] out_26,
  output [31:0] out_27,
  output [31:0] out_28,
  output [31:0] out_29,
  output [31:0] out_30,
  output [31:0] OutProc,
  output [31:0] out_32,
  output [31:0] out_33,
  output [31:0] out_34,
  output [31:0] out_35,
  output [31:0] out_36
);

  wire decoder_1_out0, decoder_1_out1, decoder_1_out2, decoder_1_out3, decoder_1_out4, decoder_1_out5,
       decoder_1_out6, decoder_1_out7, decoder_1_out8, decoder_1_out9, decoder_1_out10, decoder_1_out11,
       decoder_1_out12, decoder_1_out13, decoder_1_out14, decoder_1_out15;

  Decoder #(.select(4)) decoder_1 (
    .out0(decoder_1_out0), .out1(decoder_1_out1), .out2(decoder_1_out2), .out3(decoder_1_out3),
    .out4(decoder_1_out4), .out5(decoder_1_out5), .out6(decoder_1_out6), .out7(decoder_1_out7),
    .out8(decoder_1_out8), .out9(decoder_1_out9), .out10(decoder_1_out10), .out11(decoder_1_out11),
    .out12(decoder_1_out12), .out13(decoder_1_out13), .out14(decoder_1_out14), .out15(decoder_1_out15),
    .sel(Address), .en(in_3));
  Multiplexer #(.enable("true"), .select(4), .width(32)) multiplexer_1 (
    .in0(in_4), .in1(in_5), .in2(in_6), .in3(in_7), .in4(in_8), .in5(in_9), .in6(in_10), .in7(in_11),
    .in8(in_12), .in9(in_13), .in10(in_14), .in11(in_15), .in12(in_16), .in13(in_17), .in14(in_18),
    .in15(in_19), .out(OutProc), .en(in_3));  // open: sel
  Multiplexer #(.width(32)) multiplexer_2 (.in0({32{1'b0}}), .in1(DataIn), .out(out_20), .sel(decoder_1_out0));
  Multiplexer #(.width(32)) multiplexer_3 (.in0({32{1'b0}}), .in1(DataIn), .out(out_21), .sel(decoder_1_out1));
  Multiplexer #(.width(32)) multiplexer_4 (.in0({32{1'b0}}), .in1(DataIn), .out(out_22), .sel(decoder_1_out2));
  Multiplexer #(.width(32)) multiplexer_5 (.in0({32{1'b0}}), .in1(DataIn), .out(out_23), .sel(decoder_1_out3));
  Multiplexer #(.width(32)) multiplexer_6 (.in0({32{1'b0}}), .in1(DataIn), .out(out_24), .sel(decoder_1_out4));
  Multiplexer #(.width(32)) multiplexer_7 (.in0({32{1'b0}}), .in1(DataIn), .out(out_25), .sel(decoder_1_out5));
  Multiplexer #(.width(32)) multiplexer_8 (.in0({32{1'b0}}), .in1(DataIn), .out(out_26), .sel(decoder_1_out6));
  Multiplexer #(.width(32)) multiplexer_9 (.in0({32{1'b0}}), .in1(DataIn), .out(out_27), .sel(decoder_1_out7));
  Multiplexer #(.width(32)) multiplexer_10 (.in0({32{1'b0}}), .in1(DataIn), .out(out_28), .sel(decoder_1_out8));
  Multiplexer #(.width(32)) multiplexer_11 (.in0({32{1'b0}}), .in1(DataIn), .out(out_29), .sel(decoder_1_out9));
  Multiplexer #(.width(32)) multiplexer_12 (.in0({32{1'b0}}), .in1(DataIn), .out(out_30), .sel(decoder_1_out10));
  Multiplexer #(.width(32)) multiplexer_13 (.in0({32{1'b0}}), .in1(DataIn), .out(out_32), .sel(decoder_1_out11));
  Multiplexer #(.width(32)) multiplexer_14 (.in0({32{1'b0}}), .in1(DataIn), .out(out_33), .sel(decoder_1_out12));
  Multiplexer #(.width(32)) multiplexer_15 (.in0({32{1'b0}}), .in1(DataIn), .out(out_34), .sel(decoder_1_out13));
  Multiplexer #(.width(32)) multiplexer_16 (.in0({32{1'b0}}), .in1(DataIn), .out(out_35), .sel(decoder_1_out14));
  Multiplexer #(.width(32)) multiplexer_17 (.in0({32{1'b0}}), .in1(DataIn), .out(out_36), .sel(decoder_1_out15));
endmodule
