// Logisim project test_generic_device.circ as structural Verilog: 4 circuits, main circuit main
module main (
);

  wire and_1_out, busendpoint_3_p2, busendpoint_3_p4, busendpoint_3_p6, busendpoint_3_p8, busendpoint_4_p3,
       CLK_out, comparator_1_eq, control_1_alusrc, control_1_memwrite, control_1_op0, control_1_pcorreg,
       control_1_pcsrc, control_1_regwrite, genericindevice_1_p4, mie_q, not_1_out, ram_1_p1, ram_1_p2,
       riscvalu_1_p4, RST_out, tap_3_p1, tap_4_p1, tap_5_p1, tap_6_p1, tap_7_p1, tap_8_p1, tap_8_p3,
       undriven_2, undriven_3, undriven_4, undriven_5, undriven_6;
  wire [1:0] control_1_resultsrc;
  wire [2:0] control_1_alucontrol, control_1_immsrc, mcause_q, tap_2_p1, undriven;
  wire [3:0] tap_9_p2;
  wire [6:0] tap_1_p2;
  wire [7:0] counter_1_q, ram_1_p8, ram_1_p9, ram_1_p10, ram_1_p11, tap_1_p1, tap_1_p1_2, tap_1_p1_3,
       tap_1_p1_4;
  wire [31:0] adder_1_out, adder_2_out, busendpoint_1_p1, busendpoint_1_p3, busendpoint_1_p4,
       busendpoint_1_p12, mepc_q, mtvec_q, multiplexer_1_out, multiplexer_2_out, multiplexer_3_out, PC,
       registerfile32_1_p1, registerfile32_1_p3, riscvalu_1_p2, riscvse_j_1_p4, undriven_7;

  Adder #(.width(32)) adder_1 (.a(PC), .b(32'h4), .out(adder_1_out));  // open: cin, cout
  Button RST (.out(RST_out));
  Clock CLK (.out(CLK_out));
  Comparator #(.width(32)) comparator_1 (.a(PC), .b(32'hffff), .eq(comparator_1_eq));  // open: gt, lt
  Multiplexer #(.width(32)) multiplexer_1 (
    .in0(adder_1_out), .in1(adder_2_out), .out(multiplexer_1_out), .sel(control_1_pcsrc));
  and and_1 (and_1_out, CLK_out, not_1_out);
  not not_1 (not_1_out, comparator_1_eq);
  Register #(.width(32)) u_PC (.D(multiplexer_1_out), .Q(PC), .clk(and_1_out), .clr(RST_out));  // open: en
  // ROM #(.addrWidth(32), .line("quad")) rom_1: pin names not known; wires that end beside it: PC
  // Probe on counter_1_q
  Counter counter_1 (.Q(counter_1_q), .up(1'b1), .clk(and_1_out), .clr(RST_out));  // open: load, D, count, carry
  // RAM #(.addrWidth(32), .enables("line"), .line("quad"), .\type ("nonvolatile")) ram_1: pin names not known; wires that end beside it: ram_1_p1, ram_1_p2, 1'b1, 1'b1, 1'b1, 1'b1, and_1_out, ram_1_p8, ram_1_p9, ram_1_p10, ram_1_p11
  // Tap #(.incoming(32), .to(6)) tap_1: pin names not known; wires that end beside it: {tap_1_p1_4, tap_1_p1_3, tap_1_p1_2, tap_1_p1}, tap_1_p2
  // Tap #(.from(12), .incoming(32), .to(14)) tap_2: pin names not known; wires that end beside it: tap_2_p1
  // Tap #(.from(30), .incoming(32), .to(30)) tap_3: pin names not known; wires that end beside it: tap_3_p1
  control control_1 (
    .Funct7(tap_3_p1), .Funct3(tap_2_p1), .Zero(riscvalu_1_p4), .Op(tap_1_p2), .PCSrc(control_1_pcsrc),
    .PcOrReg(control_1_pcorreg), .ResultSrc(control_1_resultsrc), .MemWrite(control_1_memwrite),
    .ALUSrc(control_1_alusrc), .ImmSrc(control_1_immsrc), .RegWrite(control_1_regwrite), .Op0(control_1_op0),
    .ALUControl(control_1_alucontrol));  // open: O1
  // Tap #(.from(15), .incoming(32), .to(19)) tap_4: pin names not known; wires that end beside it: tap_4_p1, tap_4_p1
  // Tap #(.from(20), .incoming(32), .to(24)) tap_5: pin names not known; wires that end beside it: tap_5_p1, tap_5_p1
  // Tap #(.from(7), .incoming(32), .to(11)) tap_6: pin names not known; wires that end beside it: tap_6_p1, tap_6_p1
  // Tap #(.from(7), .incoming(32), .to(31)) tap_7: pin names not known; wires that end beside it: tap_7_p1
  // BusEndpoint #(.addressRangeEnd('hfffffff0), .addressRangeStart('h0)) busendpoint_1: pin names not known; wires that end beside it: busendpoint_1_p1, control_1_memwrite, busendpoint_1_p3, busendpoint_1_p4, control_1_memwrite, ram_1_p2, busendpoint_1_p3, ram_1_p1, busendpoint_1_p1, {ram_1_p8, ram_1_p9, ram_1_p10, ram_1_p11}, busendpoint_1_p4, busendpoint_1_p12
  // RiscvSE_J riscvse_j_1: pin names not known; wires that end beside it: tap_7_p1, control_1_immsrc, RST_out, riscvse_j_1_p4, and_1_out
  // RegisterFile32 #(.clear("baremetal")) registerfile32_1: pin names not known; wires that end beside it: registerfile32_1_p1, control_1_regwrite, registerfile32_1_p3, busendpoint_1_p1
  // BusEndpoint #(.addressRangeEnd('hfffffff1), .addressRangeStart('hfffffff0)) busendpoint_2: pin names not known; wires that end beside it: busendpoint_1_p3, busendpoint_1_p1
  // Tap #(.incoming(32)) tap_8: pin names not known; wires that end beside it: tap_8_p1, tap_8_p1, tap_8_p3
  LED led_1 (.in(tap_8_p3));
  Multiplexer #(.width(32)) multiplexer_2 (
    .in0(registerfile32_1_p3), .in1({32{1'b0}}), .out(multiplexer_2_out), .sel(control_1_op0));
  Multiplexer #(.width(32)) multiplexer_3 (
    .in0(PC), .in1(registerfile32_1_p3), .out(multiplexer_3_out), .sel(control_1_pcorreg));
  LED led_2 (.in(genericindevice_1_p4));
  // RiscvALU riscvalu_1: pin names not known; wires that end beside it: multiplexer_2_out, riscvalu_1_p2, control_1_alucontrol, riscvalu_1_p4, busendpoint_1_p3
  Multiplexer #(.width(32)) multiplexer_4 (
    .in0(busendpoint_1_p1), .in1(riscvse_j_1_p4), .out(riscvalu_1_p2), .sel(control_1_alusrc));
  Adder #(.width(32)) adder_2 (.a(multiplexer_3_out), .b(riscvse_j_1_p4), .out(adder_2_out));  // open: cin, cout
  // BusEndpoint #(.addressRangeEnd('hfffffff4), .addressRangeStart('hfffffff1)) busendpoint_3: pin names not known; wires that end beside it: control_1_memwrite, busendpoint_3_p2, busendpoint_1_p3, busendpoint_3_p4, busendpoint_1_p1, busendpoint_3_p6, busendpoint_1_p4, busendpoint_3_p8
  // GenericInDevice genericindevice_1: pin names not known; wires that end beside it: RST_out, and_1_out, busendpoint_3_p2, genericindevice_1_p4, busendpoint_3_p4, busendpoint_3_p6, busendpoint_3_p8
  // BusEndpoint #(.addressRangeEnd('hfffffff5), .addressRangeStart('hfffffff4)) busendpoint_4: pin names not known; wires that end beside it: busendpoint_1_p3, busendpoint_1_p1, busendpoint_4_p3, busendpoint_1_p1, control_1_memwrite, busendpoint_1_p3
  // Tap #(.incoming(32), .to(3)) tap_9: pin names not known; wires that end beside it: busendpoint_4_p3, tap_9_p2
  Hex_Digit_Display hex_digit_display_1 (.value(tap_9_p2));  // open: dp
  Register #(.width(3)) mcause (.D(undriven), .en(undriven_2), .Q(mcause_q), .clk(RST_out), .clr(and_1_out));
  Register #(.width(1)) mie (.D(undriven_3), .en(undriven_4), .Q(mie_q), .clk(RST_out), .clr(and_1_out));
  Register #(.width(32)) mtvec (.D(undriven_7), .en(undriven_6), .Q(mtvec_q), .clk(RST_out), .clr(and_1_out));
  Register #(.width(32)) mepc (.D(PC), .en(undriven_5), .Q(mepc_q), .clk(RST_out), .clr(and_1_out));
  Multiplexer #(.select(2), .width(32)) multiplexer_5 (
    .in0(busendpoint_1_p3), .in1(busendpoint_1_p4), .in2(adder_1_out), .out(registerfile32_1_p1));  // open: in3, sel

  // Notes on the sheet:
  //   contents of rom_1 (hex, n*v repeats v):
  //   5 c0 0 6f fe 1 1 13 0 81 2e 23 2 1 4 13 fe a4 26 23 fe b4 24 23 fe c4 27 83 fe 84 27 3 0 e7 a0 23 0
  //   0 0 13 1 c1 24 3 2 1 1 13 0 0 80 67 fe 1 1 13 0 81 2e 23 2 1 4 13 fe a4 26 23 fe c4 27 83 0 7 a7 83
  //   0 7 85 13 1 c1 24 3 2 1 1 13 0 0 80 67 fe 1 1 13 0 11 2e 23 0 81 2c 23 2 1 4 13 0 40 27 83 0 10 5 93
  //   0 7 85 13 f8 df f0 ef 0 0 27 83 0 10 5 93 0 7 85 13 f7 df f0 ef 0 0 0 13 0 80 27 83 0 7 85 13 f9 df
  //   f0 ef 0 5 7 13 0 20 7 93 fe f7 16 e3 0 40 27 83 0 7 85 13 f8 5f f0 ef fe a4 26 23 0 c0 27 83 fe c4
  //   25 83 0 7 85 13 f4 1f f0 ef 0 0 7 93 0 7 85 13 1 c1 20 83 1 81 24 3 2 1 1 13 0 0 80 67
  //   Data Bus (Out)
  //   Write Signal
  //   Address Bus
  //   Data Bus (In)
endmodule

module control (
  input  Zero,
  input  [6:0] Op,
  input  [2:0] Funct3,
  input  Funct7,
  output PCSrc,
  output PcOrReg,
  output [1:0] ResultSrc,
  output MemWrite,
  output ALUSrc,
  output [2:0] ImmSrc,
  output RegWrite,
  output Op0,
  output O1,
  output [2:0] ALUControl
);

  wire and_1_out, multiplexer_1_out, not_1_out, riscvmaindecoderext_1_p2, riscvmaindecoderext_1_p3,
       riscvmaindecoderext_1_p5, tap_1_p1, tap_2_p1;

  // Tap #(.from(5), .incoming(7), .to(5)) tap_1: pin names not known; wires that end beside it: tap_1_p1, Op
  // Tap #(.incoming(3)) tap_2: pin names not known; wires that end beside it: tap_2_p1, tap_1_p1
  not not_1 (not_1_out, Zero);
  Multiplexer multiplexer_1 (.in0(Zero), .in1(not_1_out), .out(multiplexer_1_out), .sel(tap_2_p1));
  // RiscvMainDecoderExt #(.behavior("long Op = state.getPortValue(nameToId.get(\"Op\")).toLongValue();\nlong Funct3 = state.getPortValue(nameToId.get(\"Funct3\")).toLongValue();\nlong RegWrite = 0, ImmSrc = 0, ALUSrc = 0, MemWrite = 0, ResultSrc = 0, Branch = 0, ALUOp = 0, O1 = 0, Op0=0, Jump=0, PcOrReg=0;\n\nif(Op == 0x3) { // lw\n    RegWrite = 1;\n    ALUSrc = 1;\n    ResultSrc = 1;\n} else if(Op == 0x23) { // sw\n    ImmSrc = 1;\n    ALUSrc = 1;\n    MemWrite = 1;\n} else if(Op == 0x33) { // R-type\n    RegWrite = 1;\n    ALUOp = 2;\n} else if(Op == 0x63) { // beq\n    ImmSrc = 2;\n    Branch = 1;\n    ALUOp = 1;\n} else if(Op == 0x13) { // addi\n    RegWrite = 1;\n    ALUSrc = 1;\n    ResultSrc = 0;\n    ALUOp = 2;\n} else if(Op == 0x37) { //lui\n     Op0=1;\n     RegWrite = 1;\n     ALUOp = 2;\n     ALUSrc = 1;\n     ImmSrc=3;\n} else if(Op == 0x6F) { //jal\n     RegWrite=1;\n     ImmSrc=4;\n     ResultSrc=2;\n     Jump=1;\n} else if(Op == 0x67) { //jalr\n     RegWrite=1;\n     ResultSrc=2;\n     Jump=1;\n     PcOrReg=1;\n}\n\nValue branchVal = Value.createKnown(BitWidth.create(1), Branch);\nstate.setPort(nameToId.get(\"Branch\"), branchVal, 1);\nValue resultSrcVal = Value.createKnown(BitWidth.create(2), ResultSrc);\nstate.setPort(nameToId.get(\"ResultSrc\"), resultSrcVal, 2);\nValue memWriteVal = Value.createKnown(BitWidth.create(1), MemWrite);\nstate.setPort(nameToId.get(\"MemWrite\"), memWriteVal, 1);\nValue aluSrcVal = Value.createKnown(BitWidth.create(1), ALUSrc);\nstate.setPort(nameToId.get(\"ALUSrc\"), aluSrcVal, 1);\nValue regWriteVal = Value.createKnown(BitWidth.create(1), RegWrite);\nstate.setPort(nameToId.get(\"RegWrite\"), regWriteVal, 1);\nValue immSrcVal = Value.createKnown(BitWidth.create(3), ImmSrc);\nstate.setPort(nameToId.get(\"ImmSrc\"), immSrcVal, 3);\nValue o1Val = Value.createKnown(BitWidth.create(1), O1);\nstate.setPort(nameToId.get(\"O1\"), o1Val, 1);\nValue op0Val = Value.createKnown(BitWidth.create(1), Op0);\nstate.setPort(nameToId.get(\"Op0\"), op0Val, 1);\nValue jumpVal = Value.createKnown(BitWidth.create(1), Jump);\nstate.setPort(nameToId.get(\"Jump\"), jumpVal, 1);\nValue pcOrRegVal = Value.createKnown(BitWidth.create(1), PcOrReg);\nstate.setPort(nameToId.get(\"PcOrReg\"), pcOrRegVal, 1);\nValue aluOpVal = Value.createKnown(BitWidth.create(2), ALUOp);\nstate.setPort(nameToId.get(\"ALUOp\"), aluOpVal, 2);")) riscvmaindecoderext_1: pin names not known; wires that end beside it: Funct3, riscvmaindecoderext_1_p2, riscvmaindecoderext_1_p3, PcOrReg, riscvmaindecoderext_1_p5, ResultSrc, MemWrite, ALUSrc, ImmSrc, RegWrite, Op0, O1
  // RiscvALUDecoder #(.behavior("long ALUOp = state.getPortValue(nameToId.get(\"ALUOp\")).toLongValue();\nlong Op = state.getPortValue(nameToId.get(\"Op\")).toLongValue();\nlong Funct3 = state.getPortValue(nameToId.get(\"Funct3\")).toLongValue();\nlong Funct7 = state.getPortValue(nameToId.get(\"Funct7\")).toLongValue();\n\nlong ans = 0;\n \nif (ALUOp == 0x0) { // ALUOp = 00 for lw/sw\n   ans = 0b000; // ALUControl = 000 (add) \n} else if (ALUOp == 0x1) { // ALUOp = 01 for beq\n   ans = 0b001; // ALUControl = 001 (subtract) \n} else if (ALUOp == 0x2) { // ALUOp = 10 for R-type instructions\n   if (Funct3 == 0x0) { \n      if(Op == 0x1 && Funct7 == 0x1) { \n         ans = 0b001; // ALUControl = 001 (subtract)\n      } else {\n         ans = 0b000; // ALUControl = 000 (add)\n      }  \n   } else if (Funct3 == 0x2) {   \n      ans = 0b101; // ALUControl = 101 (set less than)   \n   } else if (Funct3 == 0x6) {   \n      ans = 0b011; // ALUControl = 011 (or)   \n   } else if (Funct3 == 0x7) {   \n      ans = 0b010; // ALUControl = 010 (and)   \n   }   \n}   \n \nValue ALUControl = Value.createKnown(BitWidth.create(3), ans);   \n \nstate.setPort(nameToId.get(\"ALUControl\"), ALUControl, 3);")) riscvaludecoder_1: pin names not known; wires that end beside it: Funct3, Funct7, riscvmaindecoderext_1_p3, ALUControl
  and and_1 (and_1_out, multiplexer_1_out, riscvmaindecoderext_1_p5);
  or or_1 (PCSrc, riscvmaindecoderext_1_p2, and_1_out);
endmodule

// IO Module
module I_O (
  input  [31:0] in1,
  input  writeEnable,
  input  [3:0] Address,
  input  [31:0] DataIn,
  output [31:0] out0,
  output [31:0] OutProc
);

  wire [31:0] undriven;

  device_controller device_controller_1 (
    .addrIn(Address), .devId(4'b0000), .enable(writeEnable), .devIn(undriven), .dataIn(DataIn),
    .dataOut(OutProc), .devOut(out0));
  device_controller device_controller_2 (
    .addrIn(Address), .devId(4'b0001), .enable(writeEnable), .devIn(in1), .dataIn(DataIn), .dataOut(OutProc));  // open: devOut
endmodule

module device_controller (
  input  [31:0] devIn,
  input  enable,
  input  [31:0] dataIn,
  input  [3:0] addrIn,
  input  [3:0] devId,
  output [31:0] devOut,
  output [31:0] dataOut
);

  wire and_1_out, comparator_1_eq;

  Comparator #(.width(4)) comparator_1 (.a(addrIn), .b(devId), .eq(comparator_1_eq));  // open: gt, lt
  assign dataOut = comparator_1_eq ? devIn : 32'bz;  // Controlled_Buffer controlled_buffer_1
  assign devOut = and_1_out ? dataIn : 32'bz;  // Controlled_Buffer controlled_buffer_2
  and and_1 (and_1_out, enable, comparator_1_eq);
endmodule
