// Logisim project test_interrupts.circ as structural Verilog: 4 circuits, main circuit main
module main (
);

  wire and_1_out, and_2_out, and_3_out, and_5_out, and_6_out, and_7_out, and_8_out, busendpoint_1_p2,
       busendpoint_3_p2, busendpoint_3_p4, busendpoint_3_p6, busendpoint_3_p8, busendpoint_4_p3, CLK_out,
       comparator_1_eq, comparator_2_eq, comparator_3_eq, comparator_4_eq, comparator_5_eq, comparator_6_eq,
       comparator_7_eq, control_1_alusrc, control_1_csrwrite, control_1_memwrite, control_1_mret,
       control_1_pcorreg, control_1_pcsrc, control_1_regwrite, genericindevice_1_p4, genericindevice_1_p8,
       not_1_out, not_2_out, not_3_out, or_1_out, or_2_out, platform_level_interrupt_controller_1_p4,
       ram_1_p1, ram_1_p2, riscvalu_1_p5, RST_out, tap_3_p1, tap_4_p1, tap_5_p1, tap_6_p1, tap_7_p6,
       tap_8_p1, tap_8_p3;
  wire [1:0] control_1_regluiauipc, control_1_resultsrc;
  wire [2:0] control_1_alucontrol, control_1_immsrc, tap_2_p1;
  wire [3:0] tap_9_p2;
  wire [6:0] tap_1_p1;
  wire [7:0] counter_1_q, ram_1_p8, ram_1_p9, ram_1_p10, ram_1_p11;
  wire [31:0] adder_1_out, adder_2_out, busendpoint_1_p1, busendpoint_1_p3, busendpoint_1_p4,
       busendpoint_1_p12, controlled_buffer_1_out, mcause_q, mepc_q, multiplexer_1_out, multiplexer_2_out,
       multiplexer_3_out, multiplexer_4_out, multiplexer_5_out, multiplexer_6_out, multiplexer_7_out, PC,
       platform_level_interrupt_controller_1_p5, platform_level_interrupt_controller_1_p6,
       platform_level_interrupt_controller_1_p7, platform_level_interrupt_controller_1_p8,
       platform_level_interrupt_controller_1_p9, platform_level_interrupt_controller_1_p10,
       registerfile32_1_p1, registerfile32_1_p5, riscvse_j_1_p3, tap_7_p4;

  Adder #(.width(32)) adder_1 (.a(PC), .b(32'h4), .out(adder_1_out));  // open: cin, cout
  Multiplexer #(.width(32)) multiplexer_1 (
    .in0(adder_1_out), .in1(adder_2_out), .out(multiplexer_1_out), .sel(control_1_pcsrc));
  Multiplexer #(.width(32)) multiplexer_2 (
    .in0(multiplexer_1_out), .in1(mepc_q), .out(multiplexer_2_out), .sel(control_1_mret));
  Multiplexer #(.width(32)) multiplexer_3 (
    .in0(multiplexer_2_out), .in1(platform_level_interrupt_controller_1_p10), .out(multiplexer_3_out),
    .sel(platform_level_interrupt_controller_1_p4));
  Button RST (.out(RST_out));
  Clock CLK (.out(CLK_out));
  Comparator #(.width(32)) comparator_1 (.a(PC), .b(32'hffff), .eq(comparator_1_eq));  // open: gt, lt
  Comparator #(.width(32)) comparator_2 (.a(tap_7_p4), .b({32{1'b0}}), .eq(comparator_2_eq));  // open: gt, lt
  not not_1 (not_1_out, comparator_2_eq);
  and and_1 (and_1_out, CLK_out, not_2_out);
  not not_2 (not_2_out, comparator_1_eq);
  Register #(.width(32)) u_PC (.D(multiplexer_3_out), .Q(PC), .clk(and_2_out), .clr(RST_out));  // open: en
  and and_2 (and_2_out, not_1_out, and_1_out);
  // ROM #(.addrWidth(32), .line("quad")) rom_1: pin names not known; wires that end beside it: PC
  LED led_1 (.in(comparator_2_eq));
  Counter counter_1 (.Q(counter_1_q), .up(1'b1), .clk(and_2_out), .clr(RST_out));  // open: load, D, count, carry
  // RAM #(.addrWidth(32), .enables("line"), .line("quad"), .\type ("nonvolatile")) ram_1: pin names not known; wires that end beside it: ram_1_p1, ram_1_p2, 1'b1, 1'b1, 1'b1, 1'b1, and_2_out, ram_1_p8, ram_1_p9, ram_1_p10, ram_1_p11
  // Probe on counter_1_q
  // BusEndpoint #(.addressRangeEnd('hfffffff0), .addressRangeStart('h0)) busendpoint_1: pin names not known; wires that end beside it: busendpoint_1_p1, busendpoint_1_p2, busendpoint_1_p3, busendpoint_1_p4, busendpoint_1_p2, ram_1_p2, busendpoint_1_p3, ram_1_p1, busendpoint_1_p1, {ram_1_p8, ram_1_p9, ram_1_p10, ram_1_p11}, busendpoint_1_p4, busendpoint_1_p12
  // Tap #(.incoming(32), .to(6)) tap_1: pin names not known; wires that end beside it: tap_1_p1
  // Tap #(.from(12), .incoming(32), .to(14)) tap_2: pin names not known; wires that end beside it: tap_2_p1
  // Tap #(.from(30), .incoming(32), .to(30)) tap_3: pin names not known; wires that end beside it: tap_3_p1
  // Tap #(.from(15), .incoming(32), .to(19)) tap_4: pin names not known; wires that end beside it: tap_4_p1, tap_4_p1
  // Tap #(.from(20), .incoming(32), .to(24)) tap_5: pin names not known; wires that end beside it: tap_5_p1, tap_5_p1
  // Tap #(.from(7), .incoming(32), .to(11)) tap_6: pin names not known; wires that end beside it: tap_6_p1, tap_6_p1
  // Tap #(.from(7), .incoming(32), .to(31)) tap_7: pin names not known; wires that end beside it: tap_7_p4[31:24], tap_7_p4[23:16], tap_7_p4[15:8], tap_7_p4[7:0], tap_7_p4, tap_7_p6
  control control_1 (
    .Funct7(tap_3_p1), .Funct3(tap_2_p1), .Zero(riscvalu_1_p5), .Op(tap_1_p1), .PCSrc(control_1_pcsrc),
    .PcOrReg(control_1_pcorreg), .ResultSrc(control_1_resultsrc), .MemWrite(control_1_memwrite),
    .ALUSrc(control_1_alusrc), .ImmSrc(control_1_immsrc), .RegWrite(control_1_regwrite),
    .RegLuiAuipc(control_1_regluiauipc), .CsrWrite(control_1_csrwrite), .Mret(control_1_mret),
    .ALUControl(control_1_alucontrol));  // open: O1
  // BusEndpoint #(.addressRangeEnd('hfffffff1), .addressRangeStart('hfffffff0)) busendpoint_2: pin names not known; wires that end beside it: busendpoint_1_p3, busendpoint_1_p1
  not not_3 (not_3_out, platform_level_interrupt_controller_1_p4);
  and and_3 (and_3_out, not_3_out, control_1_regwrite);
  // RegisterFile32 #(.clear("baremetal")) registerfile32_1: pin names not known; wires that end beside it: registerfile32_1_p1, RST_out, and_2_out, and_3_out, registerfile32_1_p5, busendpoint_1_p1
  // Tap #(.incoming(32)) tap_8: pin names not known; wires that end beside it: tap_8_p1, tap_8_p1, tap_8_p3
  LED led_2 (.in(tap_8_p3));
  // RiscvSE_J riscvse_j_1: pin names not known; wires that end beside it: tap_7_p6, control_1_immsrc, riscvse_j_1_p3, riscvse_j_1_p3
  LED led_3 (.in(genericindevice_1_p4));
  Multiplexer #(.width(32)) multiplexer_4 (
    .in0(PC), .in1(registerfile32_1_p5), .out(multiplexer_4_out), .sel(control_1_pcorreg));
  // BusEndpoint #(.addressRangeEnd('hfffffff4), .addressRangeStart('hfffffff1)) busendpoint_3: pin names not known; wires that end beside it: busendpoint_1_p2, busendpoint_3_p2, busendpoint_1_p3, busendpoint_3_p4, busendpoint_1_p1, busendpoint_3_p6, busendpoint_1_p4, busendpoint_3_p8
  // GenericInDevice genericindevice_1: pin names not known; wires that end beside it: RST_out, and_2_out, busendpoint_3_p2, genericindevice_1_p4, busendpoint_3_p4, busendpoint_3_p6, busendpoint_3_p8, genericindevice_1_p8
  Multiplexer #(.select(2), .width(32)) multiplexer_5 (
    .in0(registerfile32_1_p5), .in1(PC), .in2({32{1'b0}}), .out(multiplexer_5_out));  // open: in3, sel
  Multiplexer #(.width(32)) multiplexer_6 (
    .in0(busendpoint_1_p1), .in1(riscvse_j_1_p3), .out(multiplexer_6_out), .sel(control_1_alusrc));
  Adder #(.width(32)) adder_2 (.a(riscvse_j_1_p3), .b(multiplexer_4_out), .out(adder_2_out));  // open: cin, cout
  // RiscvALU riscvalu_1: pin names not known; wires that end beside it: control_1_regluiauipc, multiplexer_5_out, multiplexer_6_out, control_1_alucontrol, riscvalu_1_p5, busendpoint_1_p3
  // BusEndpoint #(.addressRangeEnd('hfffffff5), .addressRangeStart('hfffffff4)) busendpoint_4: pin names not known; wires that end beside it: busendpoint_1_p3, busendpoint_1_p1, busendpoint_4_p3, busendpoint_1_p1, busendpoint_1_p2, busendpoint_1_p3
  and and_4 (busendpoint_1_p2, not_3_out, control_1_memwrite);
  Hex_Digit_Display hex_digit_display_1 (.value(tap_9_p2));  // open: dp
  // Tap #(.incoming(32), .to(3)) tap_9: pin names not known; wires that end beside it: busendpoint_4_p3, tap_9_p2
  and and_5 (and_5_out, not_3_out, control_1_mret);
  and and_6 (and_6_out, not_3_out, control_1_csrwrite);
  // Platform_Level_Interrupt_Controller #(.behavior("long Int0 = state.getPortValue(nameToId.get(\"Int0\")).toLongValue();\nlong Int1 = state.getPortValue(nameToId.get(\"Int1\")).toLongValue();\nlong Int2 = state.getPortValue(nameToId.get(\"Int2\")).toLongValue();\nlong Int3 = state.getPortValue(nameToId.get(\"Int3\")).toLongValue();\nlong RoutAddr = state.getPortValue(nameToId.get(\"RoutAddr\")).toLongValue();\nlong ReadMip = state.getPortValue(nameToId.get(\"ReadMip\")).toLongValue();\nlong ReadMie = state.getPortValue(nameToId.get(\"ReadMie\")).toLongValue();\nlong Mret = state.getPortValue(nameToId.get(\"Mret\")).toLongValue();\nlong Cause=0, HandleI=0, WriteMip=ReadMip, Int0_s=0, Int1_s=0, Int2_s=0, Int3_s=0, WriteMie=ReadMie;\n\n\nif(Mret==1)\n{\n	Int0_s=1;\n	WriteMie|=0x800;\n	Cause=0;\n	WriteMip&=~0x800;\n}\n\nif(Int0==1 || Int1==1 || Int2==1 || Int3==1) //Ojo, las entradas al aire tienen, valor undefined. Si usas !=0 la lías.\n{\n	System.out.println(\"AAAAAAAAAAAAAAAAAAA\");\n	WriteMip|=0x800;\n	if((ReadMie & 0x800)!=0)\n	{\n		HandleI=1;\n		WriteMie&=~0x800;\n		Cause=0x80000800;\n		Int0_s=0;\n	}\n}\n\n\nValue CauseVal = Value.createKnown(BitWidth.create(32), Cause);\nstate.setPort(nameToId.get(\"Cause\"), CauseVal, 1);\nValue HandleIVal = Value.createKnown(BitWidth.create(1), HandleI);\nstate.setPort(nameToId.get(\"HandleI\"), HandleIVal, 1);\nValue WriteMipVal = Value.createKnown(BitWidth.create(32), WriteMip);\nstate.setPort(nameToId.get(\"WriteMip\"), WriteMipVal, 1);\nValue Int0_sVal = Value.createKnown(BitWidth.create(1), Int0_s);\nstate.setPort(nameToId.get(\"Int0_s\"),Int0_sVal, 1);\nValue Int1_sVal = Value.createKnown(BitWidth.create(1), Int1_s);\nstate.setPort(nameToId.get(\"Int1_s\"), Int1_sVal, 1);\nValue Int2_sVal = Value.createKnown(BitWidth.create(1), Int2_s);\nstate.setPort(nameToId.get(\"Int2_s\"), Int2_sVal, 1);\nValue Int3_sVal = Value.createKnown(BitWidth.create(1), Int3_s);\nstate.setPort(nameToId.get(\"Int3_s\"), Int3_sVal, 1);\nValue WriteMieVal = Value.createKnown(BitWidth.create(32), WriteMie);\nstate.setPort(nameToId.get(\"WriteMie\"), WriteMieVal, 1);")) platform_level_interrupt_controller_1: pin names not known; wires that end beside it: genericindevice_1_p4, genericindevice_1_p8, and_5_out, platform_level_interrupt_controller_1_p4, platform_level_interrupt_controller_1_p5, platform_level_interrupt_controller_1_p6, platform_level_interrupt_controller_1_p7, platform_level_interrupt_controller_1_p8, platform_level_interrupt_controller_1_p9, platform_level_interrupt_controller_1_p10
  or or_1 (or_1_out, and_5_out, platform_level_interrupt_controller_1_p4);
  Comparator #(.width(32)) comparator_3 (.a(riscvse_j_1_p3), .b(32'h342), .eq(comparator_3_eq));  // open: gt, lt
  Comparator #(.width(32)) comparator_4 (.a(riscvse_j_1_p3), .b(32'h304), .eq(comparator_4_eq));  // open: gt, lt
  Comparator #(.width(32)) comparator_5 (.a(riscvse_j_1_p3), .b(32'h344), .eq(comparator_5_eq));  // open: gt, lt
  Comparator #(.width(32)) comparator_6 (.a(riscvse_j_1_p3), .b(32'h305), .eq(comparator_6_eq));  // open: gt, lt
  Comparator #(.width(32)) comparator_7 (.a(riscvse_j_1_p3), .b(32'h341), .eq(comparator_7_eq));  // open: gt, lt
  and and_7 (and_7_out, and_6_out, comparator_4_eq);
  or or_2 (or_2_out, or_1_out, and_7_out);
  and and_8 (and_8_out, and_6_out, comparator_6_eq);
  Multiplexer #(.width(32)) multiplexer_7 (
    .in0(multiplexer_5_out), .in1(platform_level_interrupt_controller_1_p7), .out(multiplexer_7_out),
    .sel(or_1_out));
  Multiplexer #(.select(2), .width(32)) multiplexer_8 (
    .in0(busendpoint_1_p3), .in1(busendpoint_1_p4), .in2(adder_1_out), .in3(controlled_buffer_1_out),
    .out(registerfile32_1_p1));  // open: sel
  assign controlled_buffer_1_out = comparator_3_eq ? mcause_q : 32'bz;  // Controlled_Buffer controlled_buffer_1
  Register #(.width(32)) mcause (
    .D(platform_level_interrupt_controller_1_p5), .en(or_1_out), .Q(mcause_q), .clk(and_2_out), .clr(RST_out));
  Register #(.width(32)) mie (
    .D(multiplexer_7_out), .en(or_2_out), .Q(platform_level_interrupt_controller_1_p6), .clk(and_2_out),
    .clr(RST_out));
  Register #(.width(32)) mip (
    .D(platform_level_interrupt_controller_1_p9), .Q(platform_level_interrupt_controller_1_p8),
    .clk(and_2_out), .clr(RST_out));  // open: en
  Register #(.width(32)) mtvec (
    .D(multiplexer_5_out), .en(and_8_out), .Q(platform_level_interrupt_controller_1_p10), .clk(and_2_out),
    .clr(RST_out));
  Register #(.width(32)) mepc (
    .D(PC), .en(platform_level_interrupt_controller_1_p4), .Q(mepc_q), .clk(and_2_out), .clr(RST_out));
  assign controlled_buffer_1_out = comparator_4_eq ? platform_level_interrupt_controller_1_p6 : 32'bz;  // Controlled_Buffer controlled_buffer_2
  assign controlled_buffer_1_out = comparator_5_eq ? platform_level_interrupt_controller_1_p8 : 32'bz;  // Controlled_Buffer controlled_buffer_3
  assign controlled_buffer_1_out = comparator_6_eq ? platform_level_interrupt_controller_1_p10 : 32'bz;  // Controlled_Buffer controlled_buffer_4
  assign controlled_buffer_1_out = comparator_7_eq ? mepc_q : 32'bz;  // Controlled_Buffer controlled_buffer_5

  // Notes on the sheet:
  //   contents of rom_1 (hex, n*v repeats v):
  //   0 0 2 97 f c2 82 93 30 52 90 73 0 0 12 b7 aa a2 82 93 30 42 90 73 6 0 0 ef f c0 0 6f fe 1 1 13 0 81
  //   2e 23 2 1 4 13 fe a4 26 23 fe b4 24 23 fe c4 27 83 fe 84 27 3 0 e7 a0 23 0 0 0 13 1 c1 24 3 2 1 1 13
  //   0 0 80 67 fe 1 1 13 0 81 2e 23 2 1 4 13 fe a4 26 23 fe c4 27 83 0 7 a7 83 0 7 85 13 1 c1 24 3 2 1 1
  //   13 0 0 80 67 fe 1 1 13 0 11 2e 23 0 81 2c 23 2 1 4 13 0 40 27 83 0 10 5 93 0 7 85 13 f8 df f0 ef 0 0
  //   27 83 0 10 5 93 0 7 85 13 f7 df f0 ef 0 0 0 13 0 80 27 83 0 7 85 13 f9 df f0 ef 0 5 7 13 0 20 7 93
  //   fe f7 16 e3 0 40 27 83 0 7 85 13 f8 5f f0 ef fe a4 26 23 0 c0 27 83 fe c4 25 83 0 7 85 13 f4 1f f0
  //   ef 0 0 7 93 0 7 85 13 1 c1 20 83 1 81 24 3 2 1 1 13 0 0 80 67 ff 1 1 13 0 81 26 23 1 1 4 13 0 0 0 13
  //   0 c1 24 3 1 1 1 13 30 20 0 73 0 0 0 13
  //   Data Bus (Out)
  //   Write Signal
  //   Address Bus
  //   Data Bus (In)
  //   Finished?
endmodule

module control (
  input  Zero,
  input  [6:0] Op,
  input  [2:0] Funct3,
  input  Funct7,
  output PCSrc,
  output PcOrReg,
  output [1:0] ResultSrc,
  output MemWrite,
  output ALUSrc,
  output [2:0] ImmSrc,
  output RegWrite,
  output [1:0] RegLuiAuipc,
  output CsrWrite,
  output Mret,
  output O1,
  output [2:0] ALUControl
);

  wire and_1_out, multiplexer_1_out, not_1_out, riscvmaindecoderext_1_p2, riscvmaindecoderext_1_p3,
       riscvmaindecoderext_1_p5, tap_1_p1, tap_2_p1;

  // Tap #(.from(5), .incoming(7), .to(5)) tap_1: pin names not known; wires that end beside it: tap_1_p1, Op
  // Tap #(.incoming(3)) tap_2: pin names not known; wires that end beside it: tap_2_p1, tap_1_p1
  not not_1 (not_1_out, Zero);
  Multiplexer multiplexer_1 (.in0(Zero), .in1(not_1_out), .out(multiplexer_1_out), .sel(tap_2_p1));
  // RiscvMainDecoderExt #(.behavior("long Op = state.getPortValue(nameToId.get(\"Op\")).toLongValue();\nlong Funct3 = state.getPortValue(nameToId.get(\"Funct3\")).toLongValue();\nlong RegWrite = 0, ImmSrc = 0, ALUSrc = 0, MemWrite = 0, ResultSrc = 0, Branch = 0, ALUOp = 0, O1 = 0, RegLuiAuipc=0, Jump=0, PcOrReg=0, CsrWrite=0, Mret=0;\n\nif(Op == 0x3) { // lw\n    RegWrite = 1;\n    ALUSrc = 1;\n    ResultSrc = 1;\n} else if(Op == 0x23) { // sw\n    ImmSrc = 1;\n    ALUSrc = 1;\n    MemWrite = 1;\n} else if(Op == 0x33) { // R-type\n    RegWrite = 1;\n    ALUOp = 2;\n} else if(Op == 0x63) { // beq\n    ImmSrc = 2;\n    Branch = 1;\n    ALUOp = 1;\n} else if(Op == 0x13) { // addi\n    RegWrite = 1;\n    ALUSrc = 1;\n    ResultSrc = 0;\n    ALUOp = 2;\n} else if(Op == 0x37) { //lui\n     RegLuiAuipc=2;\n     RegWrite = 1;\n     ALUOp = 2;\n     ALUSrc = 1;\n     ImmSrc=3;\n} else if(Op == 0x13) { //auipc\n     RegLuiAuipc=1;\n     RegWrite = 1;\n     ALUOp = 2;\n     ALUSrc = 1;\n     ImmSrc=3;\n} else if(Op == 0x6F) { //jal\n     RegWrite=1;\n     ImmSrc=4;\n     ResultSrc=2;\n     Jump=1;\n} else if(Op == 0x67) { //jalr\n     RegWrite=1;\n     ResultSrc=2;\n     Jump=1;\n     PcOrReg=1;\n}else if(Op == 0x73) { //csr\n     if(Funct3==0){ //mret\n         Mret=1;\n     }\n     if(Funct3==2){ //csrr\n         RegWrite = 1;\n         ResultSrc= 3;\n     }\n     else if(Funct3==1){ //csrw\n         CsrWrite = 1;\n     }\n}\nValue branchVal = Value.createKnown(BitWidth.create(1), Branch);\nstate.setPort(nameToId.get(\"Branch\"), branchVal, 1);\nValue resultSrcVal = Value.createKnown(BitWidth.create(2), ResultSrc);\nstate.setPort(nameToId.get(\"ResultSrc\"), resultSrcVal, 2);\nValue memWriteVal = Value.createKnown(BitWidth.create(1), MemWrite);\nstate.setPort(nameToId.get(\"MemWrite\"), memWriteVal, 1);\nValue aluSrcVal = Value.createKnown(BitWidth.create(1), ALUSrc);\nstate.setPort(nameToId.get(\"ALUSrc\"), aluSrcVal, 1);\nValue regWriteVal = Value.createKnown(BitWidth.create(1), RegWrite);\nstate.setPort(nameToId.get(\"RegWrite\"), regWriteVal, 1);\nValue immSrcVal = Value.createKnown(BitWidth.create(3), ImmSrc);\nstate.setPort(nameToId.get(\"ImmSrc\"), immSrcVal, 3);\nValue o1Val = Value.createKnown(BitWidth.create(1), O1);\nstate.setPort(nameToId.get(\"O1\"), o1Val, 1);\nValue regluiauipcVal = Value.createKnown(BitWidth.create(2), RegLuiAuipc);\nstate.setPort(nameToId.get(\"RegLuiAuipc\"), regluiauipcVal, 1);\nValue csrWriteVal = Value.createKnown(BitWidth.create(1), CsrWrite);\nstate.setPort(nameToId.get(\"CsrWrite\"), csrWriteVal, 1);\nValue jumpVal = Value.createKnown(BitWidth.create(1), Jump);\nstate.setPort(nameToId.get(\"Jump\"), jumpVal, 1);\nValue pcOrRegVal = Value.createKnown(BitWidth.create(1), PcOrReg);\nstate.setPort(nameToId.get(\"PcOrReg\"), pcOrRegVal, 1);\nValue aluOpVal = Value.createKnown(BitWidth.create(2), ALUOp);\nstate.setPort(nameToId.get(\"ALUOp\"), aluOpVal, 2);\nValue mretVal = Value.createKnown(BitWidth.create(1), Mret);\nstate.setPort(nameToId.get(\"Mret\"), mretVal, 1);")) riscvmaindecoderext_1: pin names not known; wires that end beside it: Funct3, riscvmaindecoderext_1_p2, riscvmaindecoderext_1_p3, PcOrReg, riscvmaindecoderext_1_p5, ResultSrc, MemWrite, ALUSrc, ImmSrc, RegWrite, RegLuiAuipc, CsrWrite, Mret, O1
  // RiscvALUDecoder #(.behavior("long ALUOp = state.getPortValue(nameToId.get(\"ALUOp\")).toLongValue();\nlong Op = state.getPortValue(nameToId.get(\"Op\")).toLongValue();\nlong Funct3 = state.getPortValue(nameToId.get(\"Funct3\")).toLongValue();\nlong Funct7 = state.getPortValue(nameToId.get(\"Funct7\")).toLongValue();\n\nlong ans = 0;\n \nif (ALUOp == 0x0) { // ALUOp = 00 for lw/sw\n   ans = 0b000; // ALUControl = 000 (add) \n} else if (ALUOp == 0x1) { // ALUOp = 01 for beq\n   ans = 0b001; // ALUControl = 001 (subtract) \n} else if (ALUOp == 0x2) { // ALUOp = 10 for R-type instructions\n   if (Funct3 == 0x0) { \n      if(Op == 0x1 && Funct7 == 0x1) { \n         ans = 0b001; // ALUControl = 001 (subtract)\n      } else {\n         ans = 0b000; // ALUControl = 000 (add)\n      }  \n   } else if (Funct3 == 0x2) {   \n      ans = 0b101; // ALUControl = 101 (set less than)   \n   } else if (Funct3 == 0x6) {   \n      ans = 0b011; // ALUControl = 011 (or)   \n   } else if (Funct3 == 0x7) {   \n      ans = 0b010; // ALUControl = 010 (and)   \n   }   \n}   \n \nValue ALUControl = Value.createKnown(BitWidth.create(3), ans);   \n \nstate.setPort(nameToId.get(\"ALUControl\"), ALUControl, 3);")) riscvaludecoder_1: pin names not known; wires that end beside it: Funct3, Funct7, riscvmaindecoderext_1_p3, ALUControl
  and and_1 (and_1_out, multiplexer_1_out, riscvmaindecoderext_1_p5);
  or or_1 (PCSrc, riscvmaindecoderext_1_p2, and_1_out);
endmodule

// IO Module
module I_O (
  input  [31:0] in1,
  input  writeEnable,
  input  [3:0] Address,
  input  [31:0] DataIn,
  output [31:0] out0,
  output [31:0] OutProc
);

  wire [31:0] undriven;

  device_controller device_controller_1 (
    .addrIn(Address), .devId(4'b0000), .enable(writeEnable), .devIn(undriven), .dataIn(DataIn),
    .dataOut(OutProc), .devOut(out0));
  device_controller device_controller_2 (
    .addrIn(Address), .devId(4'b0001), .enable(writeEnable), .devIn(in1), .dataIn(DataIn), .dataOut(OutProc));  // open: devOut
endmodule

module device_controller (
  input  [31:0] devIn,
  input  enable,
  input  [31:0] dataIn,
  input  [3:0] addrIn,
  input  [3:0] devId,
  output [31:0] devOut,
  output [31:0] dataOut
);

  wire and_1_out, comparator_1_eq;

  Comparator #(.width(4)) comparator_1 (.a(addrIn), .b(devId), .eq(comparator_1_eq));  // open: gt, lt
  assign dataOut = comparator_1_eq ? devIn : 32'bz;  // Controlled_Buffer controlled_buffer_1
  assign devOut = and_1_out ? dataIn : 32'bz;  // Controlled_Buffer controlled_buffer_2
  and and_1 (and_1_out, enable, comparator_1_eq);
endmodule
